# Fritzing sketch rainbow (saved by Fritzing 0.9.3b)
circuit board: 6cm x 4cm
breadboards: 1

parts:
  Part1 = Arduino Nano (Rev3.0)
  RE1 = Rotary Encoder [package=THT]
  S1 = Pushbutton [package=THT]
  R5 = Resistor [tolerance=±5% resistance=470 package="0805 [SMD]"]
  R4 = Resistor [tolerance=±5% resistance=10k package="0805 [SMD]"]
  R3 = Resistor [tolerance=±5% resistance=10k package="0805 [SMD]"]
  R2 = Resistor [tolerance=±5% resistance=10k package="0805 [SMD]"]
  C1 = Electrolytic Capacitor [capacitance=1000µF package="300 mil [THT, electrolytic]"]
  J3 = female pin header, 3 pins [form="♀ (female)"]
  T1 = Screw terminal - 2 pins [package=THT]
  T2 = Screw terminal - 2 pins [package=THT]

nets:
  GND: Part1.GND, RE1.EncoderPinC, S1.leg0, C1.-, J3.pin3, T1.pin1, T2.pin2
  N1: Part1.D6, R5.Pin_0
  N2: Part1.D9, RE1.EncoderPinB, R2.Pin_0
  N3: Part1.D10, RE1.EncoderPinA, R4.Pin_0
  N4: Part1.D11/MOSI, S1.leg1, R3.Pin_0
  N5: Part1.VIN, C1.+, J3.pin2, T1.pin2, T2.pin1
  5V: Part1.5V, R4.Pin_1, R3.Pin_1, R2.Pin_1
  N6: R5.Pin_1, J3.pin1
